// Digital circuit dmux.dig as structural Verilog
module dmux (
  input  in_1,
  input  in_4,
  input  in_9,
  input  in_12,
  input  in_25,
  output a,
  output b,
  output a_2,
  output b_2,
  output a_3,
  output b_3,
  output a_4,
  output b_4,
  output a_5,
  output b_5,
  output c,
  output d,
  output e,
  output f,
  output g,
  output h,
  output a_6,
  output b_6,
  output c_2,
  output d_2
);

  wire and_5_out, and_6_out, and_7_out, and_8_out, and_17_out, and_18_out, and_19_out, and_20_out,
       and_21_out, and_22_out, not_1_out, not_2_out, not_3_out, not_4_out, not_5_out, not_6_out, not_7_out,
       not_8_out, not_9_out, not_10_out, not_11_out, not_12_out, not_13_out, not_14_out, not_15_out,
       sel1_out, sel2_2_out, sel2_out, sel3_out, sel_2_out, sel_3_out, sel_4_out, sel_5_out, sel_out;

  not not_1 (not_1_out, sel_out);
  and and_1 (b, in_1, sel_out);
  DipSwitch sel (.out(sel_out));
  and and_2 (a, in_1, not_1_out);
  DipSwitch sel_2 (.out(sel_2_out));
  and and_3 (a_4, in_9, not_2_out);
  not not_2 (not_2_out, sel_2_out);
  and and_4 (b_4, sel_2_out, in_9);
  not not_3 (not_3_out, sel_3_out);
  and and_5 (and_5_out, in_4, sel_3_out);
  DipSwitch sel_3 (.out(sel_3_out));
  DipSwitch sel_4 (.out(sel_4_out));
  and and_6 (and_6_out, in_4, not_3_out);
  and and_7 (and_7_out, in_12, not_4_out);
  not not_4 (not_4_out, sel_4_out);
  and and_8 (and_8_out, sel_4_out, in_12);
  DipSwitch sel2 (.out(sel2_out));
  and and_9 (a_2, and_6_out, not_5_out);
  not not_5 (not_5_out, sel_5_out);
  and and_10 (b_2, and_6_out, sel_5_out);
  DipSwitch sel_5 (.out(sel_5_out));
  and and_11 (a_3, and_5_out, not_6_out);
  not not_6 (not_6_out, sel_5_out);
  and and_12 (b_3, and_5_out, sel_5_out);
  and and_13 (a_5, and_7_out, not_7_out);
  not not_7 (not_7_out, sel2_out);
  and and_14 (b_5, sel2_out, and_7_out);
  and and_15 (c, and_8_out, not_8_out);
  not not_8 (not_8_out, sel2_out);
  and and_16 (d, sel2_out, and_8_out);
  not not_9 (not_9_out, sel3_out);
  DipSwitch sel3 (.out(sel3_out));
  and and_17 (and_17_out, in_25, not_9_out);
  and and_18 (and_18_out, sel3_out, in_25);
  not not_10 (not_10_out, sel2_2_out);
  DipSwitch sel2_2 (.out(sel2_2_out));
  not not_11 (not_11_out, sel2_2_out);
  and and_19 (and_19_out, and_17_out, not_10_out);
  and and_20 (and_20_out, sel2_2_out, and_17_out);
  and and_21 (and_21_out, and_18_out, not_11_out);
  and and_22 (and_22_out, sel2_2_out, and_18_out);
  DipSwitch sel1 (.out(sel1_out));
  not not_12 (not_12_out, sel1_out);
  not not_13 (not_13_out, sel1_out);
  not not_14 (not_14_out, sel1_out);
  not not_15 (not_15_out, sel1_out);
  and and_23 (a_6, and_19_out, not_12_out);
  and and_24 (b_6, sel1_out, and_19_out);
  and and_25 (c_2, and_20_out, not_13_out);
  and and_26 (d_2, sel1_out, and_20_out);
  and and_27 (e, and_21_out, not_14_out);
  and and_28 (f, sel1_out, and_21_out);
  and and_29 (g, and_22_out, not_15_out);
  and and_30 (h, sel1_out, and_22_out);

  // Notes on the sheet:
  //   DMux
  //   DMux4way
  //   DMux8way
endmodule
