// Digital circuit mux.dig as structural Verilog
module mux (
  input  a,
  input  b,
  input  a_2,
  input  b_2,
  input  c,
  input  d,
  input  a_3,
  input  b_3,
  input  c_2,
  input  d_2,
  input  a_4,
  input  b_4,
  input  c_3,
  input  d_3,
  input  e,
  input  f,
  input  g,
  input  h,
  output out,
  output out_2,
  output out_3,
  output out_4
);

  wire and_1_out, and_2_out, and_3_out, and_4_out, and_5_out, and_6_out, and_7_out, and_8_out, and_9_out,
       and_10_out, and_11_out, and_12_out, and_13_out, and_14_out, and_15_out, and_16_out, and_17_out,
       and_18_out, and_19_out, and_20_out, and_21_out, and_22_out, and_23_out, and_24_out, and_25_out,
       and_26_out, and_27_out, and_28_out, not_1_out, not_2_out, not_3_out, not_4_out, not_5_out, not_6_out,
       not_7_out, not_8_out, not_9_out, not_10_out, not_11_out, not_12_out, not_13_out, not_14_out, sel2_out,
       sel3_out, sel5_out, sel_2_out, sel_3_out, sel_4_out, sel_5_out, sel_out, xor_2_out, xor_3_out,
       xor_5_out, xor_6_out, xor_8_out, xor_9_out, xor_10_out, xor_11_out, xor_12_out, xor_13_out;

  and and_1 (and_1_out, a, not_1_out);
  not not_1 (not_1_out, sel_out);
  and and_2 (and_2_out, b, sel_out);
  DipSwitch sel (.out(sel_out));
  xor xor_1 (out, and_1_out, and_2_out);
  and and_3 (and_3_out, a_2, not_2_out);
  not not_2 (not_2_out, sel_2_out);
  and and_4 (and_4_out, b_2, sel_2_out);
  DipSwitch sel_2 (.out(sel_2_out));
  and and_5 (and_5_out, c, not_3_out);
  not not_3 (not_3_out, sel_2_out);
  and and_6 (and_6_out, d, sel_2_out);
  xor xor_2 (xor_2_out, and_3_out, and_4_out);
  xor xor_3 (xor_3_out, and_5_out, and_6_out);
  DipSwitch sel2 (.out(sel2_out));
  and and_7 (and_7_out, xor_2_out, not_4_out);
  not not_4 (not_4_out, sel2_out);
  and and_8 (and_8_out, sel2_out, xor_3_out);
  xor xor_4 (out_2, and_7_out, and_8_out);
  and and_9 (and_9_out, a_3, not_5_out);
  not not_5 (not_5_out, sel_3_out);
  and and_10 (and_10_out, b_3, sel_3_out);
  DipSwitch sel_3 (.out(sel_3_out));
  and and_11 (and_11_out, c_2, not_6_out);
  not not_6 (not_6_out, sel_3_out);
  and and_12 (and_12_out, d_2, sel_3_out);
  xor xor_5 (xor_5_out, and_9_out, and_10_out);
  xor xor_6 (xor_6_out, and_11_out, and_12_out);
  DipSwitch sel3 (.out(sel3_out));
  and and_13 (and_13_out, xor_5_out, not_7_out);
  not not_7 (not_7_out, sel3_out);
  and and_14 (and_14_out, sel3_out, xor_6_out);
  xor xor_7 (out_3, and_13_out, and_14_out);
  DipSwitch sel_4 (.out(sel_4_out));
  not not_8 (not_8_out, sel_4_out);
  not not_9 (not_9_out, sel_4_out);
  and and_15 (and_15_out, e, not_10_out);
  not not_10 (not_10_out, sel_4_out);
  and and_16 (and_16_out, f, sel_4_out);
  and and_17 (and_17_out, g, not_11_out);
  not not_11 (not_11_out, sel_4_out);
  and and_18 (and_18_out, h, sel_4_out);
  and and_19 (and_19_out, a_4, not_8_out);
  and and_20 (and_20_out, b_4, sel_4_out);
  and and_21 (and_21_out, c_3, not_9_out);
  and and_22 (and_22_out, d_3, sel_4_out);
  xor xor_8 (xor_8_out, and_19_out, and_20_out);
  xor xor_9 (xor_9_out, and_21_out, and_22_out);
  xor xor_10 (xor_10_out, and_15_out, and_16_out);
  xor xor_11 (xor_11_out, and_17_out, and_18_out);
  DipSwitch sel5 (.out(sel5_out));
  not not_12 (not_12_out, sel5_out);
  and and_23 (and_23_out, xor_10_out, not_13_out);
  not not_13 (not_13_out, sel5_out);
  and and_24 (and_24_out, sel5_out, xor_11_out);
  and and_25 (and_25_out, xor_8_out, not_12_out);
  and and_26 (and_26_out, sel5_out, xor_9_out);
  xor xor_12 (xor_12_out, and_25_out, and_26_out);
  xor xor_13 (xor_13_out, and_23_out, and_24_out);
  not not_14 (not_14_out, sel_5_out);
  DipSwitch sel_5 (.out(sel_5_out));
  and and_27 (and_27_out, xor_12_out, not_14_out);
  and and_28 (and_28_out, xor_13_out, sel_5_out);
  xor xor_14 (out_4, and_27_out, and_28_out);

  // Notes on the sheet:
  //   Mux
  //   Mux4way
  //   Mux8way
endmodule
