// Logisim project ALU.circ as structural Verilog: 1 circuit, main circuit main
module main (
  input  zx,
  input  nx,
  input  f,
  input  no,
  input  [15:0] in_5,
  input  [15:0] x,
  input  zy,
  input  ny,
  input  [15:0] y,
  input  [15:0] in_10,
  output zr,
  output ng,
  output [15:0] outt
);

  wire or_1_out, or_2_out;
  wire [15:0] adder_1_out, and_1_out, multiplexer_1_out, multiplexer_2_out, multiplexer_3_out,
       multiplexer_4_out, multiplexer_5_out, not_1_out, not_2_out, not_3_out;

  Multiplexer #(.width(16)) multiplexer_1 (.in0(x), .in1(in_5), .out(multiplexer_1_out), .sel(zx));
  Multiplexer #(.width(16)) multiplexer_2 (.in0(y), .in1(in_10), .out(multiplexer_2_out), .sel(zy));
  assign not_1_out = ~multiplexer_1_out;  // NOT_Gate not_1, 16 bits wide
  assign not_2_out = ~multiplexer_2_out;  // NOT_Gate not_2, 16 bits wide
  Multiplexer #(.width(16)) multiplexer_3 (.in0(multiplexer_1_out), .in1(not_1_out), .out(multiplexer_3_out), .sel(nx));
  Multiplexer #(.width(16)) multiplexer_4 (.in0(multiplexer_2_out), .in1(not_2_out), .out(multiplexer_4_out), .sel(ny));
  assign and_1_out = multiplexer_3_out & multiplexer_4_out;  // AND_Gate and_1, 16 bits wide
  Adder #(.width(16)) adder_1 (.a(multiplexer_3_out), .b(multiplexer_4_out), .out(adder_1_out));  // open: cin, cout
  Multiplexer #(.width(16)) multiplexer_5 (.in0(and_1_out), .in1(adder_1_out), .out(multiplexer_5_out), .sel(f));
  assign not_3_out = ~multiplexer_5_out;  // NOT_Gate not_3, 16 bits wide
  Multiplexer #(.width(16)) multiplexer_6 (.in0(multiplexer_5_out), .in1(not_3_out), .out({ng, outt[14:0]}), .sel(no));
  or or_1 (or_1_out, outt[0], outt[1], outt[2], outt[3], outt[4], outt[5], outt[6], outt[7]);
  or or_2 (or_2_out, outt[8], outt[9], outt[10], outt[11], outt[12], outt[13], outt[14], ng);
  nor nor_1 (zr, or_1_out, or_2_out);

  assign outt[15] = ng;
endmodule
