// Logisim project Bit.circ as structural Verilog: 1 circuit, main circuit main
module main (
  input  load,
  input  set,
  output o
);

  wire multiplexer_1_out, ticktick_out;

  Clock ticktick (.out(ticktick_out));
  D_Flip_Flop DFF (.D(multiplexer_1_out), .clk(ticktick_out), .Q(o));  // open: Qn, preset, reset
  Multiplexer multiplexer_1 (.in0(o), .in1(set), .out(multiplexer_1_out), .sel(load));
endmodule
