// Logisim project DMux.circ as structural Verilog: 1 circuit, main circuit main
module main (
  input  in_1,
  input  in_2,
  input  inp,
  input  sel
);

  wire and_1_out, and_2_out, and_3_out, and_4_out, not_1_out, not_2_out;

  not not_1 (not_1_out, sel);
  and and_1 (and_1_out, inp, not_1_out);
  and and_2 (and_2_out, sel, inp);
  LED a (.in(and_1_out));
  LED b (.in(and_2_out));
  not not_2 (not_2_out, in_2);
  and and_3 (and_3_out, in_1, not_2_out);
  and and_4 (and_4_out, in_2, in_1);
  LED led_1 (.in(and_3_out));
  LED led_2 (.in(and_4_out));

  // Notes on the sheet:
  //   DMux
  //   DMux
endmodule
