// Logisim project FullAdder.circ as structural Verilog: 1 circuit, main circuit main
module main (
  input  c2,
  input  a2,
  input  b2,
  output sum2,
  output carry2
);

  wire and_1_out, and_2_out, xor_1_out;

  xor xor_1 (xor_1_out, a2, b2);
  and and_1 (and_1_out, a2, b2);
  xor xor_2 (sum2, c2, xor_1_out);
  and and_2 (and_2_out, c2, xor_1_out);
  xor xor_3 (carry2, and_2_out, and_1_out);

  // Notes on the sheet:
  //   FullAdder
endmodule
