// Logisim project HalfAdder.circ as structural Verilog: 1 circuit, main circuit main
module main (
  input  a,
  input  b,
  output sum,
  output carry
);

  xor xor_1 (sum, a, b);
  and and_1 (carry, a, b);

  // Notes on the sheet:
  //   HalfAdder
endmodule
