// Logisim project PC.circ as structural Verilog: 1 circuit, main circuit main
module main (
  input  inc,
  input  load,
  input  reset,
  input  [15:0] inputs,
  input  [15:0] in_5,
  input  [15:0] in_6,
  output [15:0] outt
);

  wire clock_1_out, or_1_out, or_2_out;
  wire [15:0] adder_1_out, multiplexer_1_out, multiplexer_2_out, multiplexer_3_out;

  Multiplexer #(.width(16)) multiplexer_1 (.in0(inputs), .in1(adder_1_out), .out(multiplexer_1_out), .sel(inc));
  Adder #(.width(16)) adder_1 (.a(in_5), .b(outt), .out(adder_1_out));  // open: cin, cout
  or or_1 (or_1_out, load, inc);
  Multiplexer #(.width(16)) multiplexer_2 (.in0(multiplexer_1_out), .in1(inputs), .out(multiplexer_2_out), .sel(load));
  or or_2 (or_2_out, or_1_out, reset);
  Multiplexer #(.width(16)) multiplexer_3 (.in0(multiplexer_2_out), .in1(in_6), .out(multiplexer_3_out), .sel(reset));
  Register #(.width(16)) register_1 (.D(multiplexer_3_out), .en(or_2_out), .clk(clock_1_out), .Q(outt));  // open: clr
  Clock clock_1 (.out(clock_1_out));
endmodule
