// Logisim project RAM8.circ as structural Verilog: 1 circuit, main circuit main
module main (
  input  [15:0] in_1,
  input  load,
  input  [2:0] address,
  output [15:0] out_4
);

  wire demultiplexer_1_out0, demultiplexer_1_out1, demultiplexer_1_out2, demultiplexer_1_out3,
       demultiplexer_1_out4, demultiplexer_1_out5, demultiplexer_1_out6, demultiplexer_1_out7;
  wire [15:0] register_1_q, register_2_q, register_3_q, register_4_q, register_5_q, register_6_q,
       register_7_q, register_8_q;

  Demultiplexer #(.select(3)) demultiplexer_1 (
    .out0(demultiplexer_1_out0), .out1(demultiplexer_1_out1), .out2(demultiplexer_1_out2),
    .out3(demultiplexer_1_out3), .out4(demultiplexer_1_out4), .out5(demultiplexer_1_out5),
    .out6(demultiplexer_1_out6), .out7(demultiplexer_1_out7), .in(load), .sel(address));
  Register #(.width(16)) register_1 (.D(in_1), .clk(demultiplexer_1_out7), .Q(register_1_q));  // open: en, clr
  Register #(.width(16)) register_2 (.D(in_1), .clk(demultiplexer_1_out3), .Q(register_2_q));  // open: en, clr
  Register #(.width(16)) register_3 (.D(in_1), .clk(demultiplexer_1_out6), .Q(register_3_q));  // open: en, clr
  Register #(.width(16)) register_4 (.D(in_1), .clk(demultiplexer_1_out2), .Q(register_4_q));  // open: en, clr
  Register #(.width(16)) register_5 (.D(in_1), .clk(demultiplexer_1_out5), .Q(register_5_q));  // open: en, clr
  Register #(.width(16)) register_6 (.D(in_1), .clk(demultiplexer_1_out1), .Q(register_6_q));  // open: en, clr
  Register #(.width(16)) register_7 (.D(in_1), .clk(demultiplexer_1_out4), .Q(register_7_q));  // open: en, clr
  Register #(.width(16)) register_8 (.D(in_1), .clk(demultiplexer_1_out0), .Q(register_8_q));  // open: en, clr
  Multiplexer #(.select(3), .width(16)) multiplexer_1 (
    .in0(register_8_q), .in1(register_6_q), .in2(register_4_q), .in3(register_2_q), .in4(register_7_q),
    .in5(register_5_q), .in6(register_3_q), .in7(register_1_q), .out(out_4), .sel(address));
endmodule
